# Fritzing sketch countBotton (saved by Fritzing 0.8.7b)
breadboards: 1

parts:
  R1 = Resistor [tolerance=±5% resistance=10k package=THT]
  S1 = Pushbutton [package="[THT]"]
  Componente1 = Arduino Mega 2560 (Rev3)
  7_Segment1 = 7 Segment Display

nets:
  N1: R1.Pin_0, S1.Pin_1, S1.Pin_2, Componente1.D10_PWM
  N2: R1.Pin_1, Componente1.GND, 7_Segment1.common_anode
  N3: S1.Pin_3, S1.Pin_4, Componente1.5V
  N4: Componente1.D9_PWM, 7_Segment1.Segment_G
  N5: Componente1.D8_PWM, 7_Segment1.Segment_F
  N6: Componente1.D2_PWM, 7_Segment1.Segment_E
  N7: Componente1.D3_PWM, 7_Segment1.Segment_D
  N8: Componente1.D4_PWM, 7_Segment1.Segment_C
  N9: Componente1.D5_PWM, 7_Segment1.Segment_DP
  N10: Componente1.D6_PWM, 7_Segment1.Segment_B
  N11: Componente1.D7_PWM, 7_Segment1.Segment_A
